// Logisim project lab3.1.circ as structural Verilog: 1 circuit, main circuit main
module main (
  input  a,
  input  b,
  input  c,
  input  d,
  input  e,
  output x
);

  wire nand_1_out, nand_2_out, nand_3_out, nand_4_out, nand_5_out, nand_6_out, nand_7_out, nand_8_out,
       nand_9_out, nand_10_out, nand_11_out, nand_12_out, nand_13_out, nand_14_out, nand_15_out;

  nand nand_1 (nand_1_out, a, a);
  nand nand_2 (nand_2_out, c, c);
  nand nand_3 (nand_3_out, b, b);
  nand nand_4 (nand_4_out, a, a);
  nand nand_5 (nand_5_out, c, c);
  nand nand_6 (nand_6_out, a, a);
  nand nand_7 (nand_7_out, d, d);
  nand nand_8 (nand_8_out, b, b);
  nand nand_9 (nand_9_out, c, c);
  nand nand_10 (nand_10_out, nand_1_out, e);
  nand nand_11 (nand_11_out, nand_2_out, e);
  nand nand_12 (nand_12_out, nand_3_out, d);
  nand nand_13 (nand_13_out, nand_4_out, b, nand_5_out);
  nand nand_14 (nand_14_out, nand_6_out, b, nand_7_out);
  nand nand_15 (nand_15_out, a, nand_8_out, nand_9_out);
  nand nand_16 (x, nand_10_out, nand_11_out, nand_12_out, nand_13_out, nand_14_out, nand_15_out);
endmodule
