// Logisim project lab5.circ as structural Verilog: 2 circuits, main circuit main
module jk (
  input  in_1,
  input  in_2,
  input  in_3,
  output out_4,
  output out_5
);

  J_K_Flip_Flop j_k_ff_1 (.Q(out_4), .Qn(out_5), .preset(in_1), .en(in_2), .reset(in_3));  // open: J, clk, K
endmodule

module main (
  input  in_1,
  input  in_2,
  input  in_3,
  input  \D_триггер ,
  input  in_5,
  input  \Т_триггер ,
  input  in_7,
  output out_8,
  output out_9,
  output out_10,
  output out_11,
  output out_12,
  output out_13
);

  wire nand_1_out, nand_2_out, nand_3_out, nand_4_out, nand_7_out, nand_8_out, nand_9_out, nand_10_out,
       xor_1_out;

  nand nand_1 (nand_1_out, \D_триггер , in_5);
  nand nand_2 (nand_2_out, nand_1_out, in_5);
  xor xor_1 (xor_1_out, in_7, out_12);
  nand nand_3 (nand_3_out, out_9, in_1, in_2);
  nand nand_4 (nand_4_out, in_2, in_3, out_8);
  nand nand_5 (out_10, nand_1_out, out_11);
  nand nand_6 (out_11, out_10, nand_2_out);
  D_Flip_Flop d_ff_1 (.clk(\Т_триггер ), .D(xor_1_out), .Q(out_12), .Qn(out_13));  // open: preset, en, reset
  nand nand_7 (nand_7_out, nand_3_out, nand_8_out);
  nand nand_8 (nand_8_out, nand_7_out, nand_4_out);
  nand nand_9 (nand_9_out, nand_3_out, nand_7_out);
  nand nand_10 (nand_10_out, nand_8_out, nand_4_out);
  nand nand_11 (out_8, nand_9_out, out_9);
  nand nand_12 (out_9, out_8, nand_10_out);

  // Notes on the sheet:
  //   jk-триггер
endmodule
